// Logisim project lab03.circ as structural Verilog: 4 circuits, main circuit ALU4
module ALU4 (
  input  [3:0] ALU_Ctrl,
  input  [3:0] A,
  input  [3:0] B,
  input  C_in,
  output [3:0] R,
  output C_out
);

  wire one_bit_alu_1_c_out, one_bit_alu_2_c_out, one_bit_alu_3_c_out;

  one_bit_ALU one_bit_alu_1 (
    .ALU_Ctrl(ALU_Ctrl), .A(A[0]), .B(B[0]), .C_in(C_in), .R(R[0]), .C_out(one_bit_alu_1_c_out));
  one_bit_ALU one_bit_alu_2 (
    .ALU_Ctrl(ALU_Ctrl), .A(A[1]), .B(B[1]), .C_in(one_bit_alu_1_c_out), .R(R[1]), .C_out(one_bit_alu_2_c_out));
  one_bit_ALU one_bit_alu_3 (
    .ALU_Ctrl(ALU_Ctrl), .A(A[2]), .B(B[2]), .C_in(one_bit_alu_2_c_out), .R(R[2]), .C_out(one_bit_alu_3_c_out));
  one_bit_ALU one_bit_alu_4 (
    .ALU_Ctrl(ALU_Ctrl), .A(A[3]), .B(B[3]), .C_in(one_bit_alu_3_c_out), .R(R[3]), .C_out(C_out));
endmodule

module one_bit_adder (
  input  A,
  input  B,
  input  Cin,
  output S,
  output Cout
);

  wire and_1_out, and_2_out, and_3_out, and_4_out, and_5_out, and_6_out, and_7_out, not_1_out, not_2_out,
       not_3_out;

  not not_1 (not_1_out, A);
  not not_2 (not_2_out, B);
  not not_3 (not_3_out, Cin);
  and and_1 (and_1_out, not_1_out, not_2_out, Cin);
  and and_2 (and_2_out, not_1_out, B, not_3_out);
  and and_3 (and_3_out, A, not_2_out, not_3_out);
  and and_4 (and_4_out, A, B, Cin);
  and and_5 (and_5_out, B, Cin);
  and and_6 (and_6_out, A, Cin);
  and and_7 (and_7_out, A, B);
  or or_1 (S, and_1_out, and_2_out, and_3_out, and_4_out);
  or or_2 (Cout, and_5_out, and_6_out, and_7_out);
endmodule

module one_bit_ALU (
  input  [3:0] ALU_Ctrl,
  input  A,
  input  B,
  input  C_in,
  output R,
  output C_out
);

  wire and_1_out, multiplexer_1_out, not_1_out, one_bit_adder_1_s, or_1_out, xor_1_out;

  not not_1 (not_1_out, B);
  Multiplexer #(.enable("false")) multiplexer_1 (.in0(B), .in1(not_1_out), .out(multiplexer_1_out), .sel(ALU_Ctrl[2]));
  and and_1 (and_1_out, A, multiplexer_1_out);
  or or_1 (or_1_out, A, multiplexer_1_out);
  xor xor_1 (xor_1_out, A, multiplexer_1_out);
  one_bit_adder one_bit_adder_1 (.A(A), .B(multiplexer_1_out), .Cin(C_in), .S(one_bit_adder_1_s), .Cout(C_out));
  Multiplexer #(.enable("false"), .select(2)) multiplexer_2 (
    .in0(and_1_out), .in1(or_1_out), .in2(xor_1_out), .in3(one_bit_adder_1_s), .out(R), .sel(ALU_Ctrl[1:0]));
endmodule

module ALU32 (
  input  [3:0] ALU_Ctrl,
  input  [31:0] A,
  input  [31:0] B,
  output [31:0] Result,
  output C_out
);

  wire alu4_1_c_out, alu4_2_c_out, alu4_3_c_out, alu4_4_c_out, alu4_5_c_out, alu4_6_c_out, alu4_7_c_out;

  ALU4 alu4_1 (.ALU_Ctrl(ALU_Ctrl), .A(A[3:0]), .B(B[3:0]), .C_in(ALU_Ctrl[2]), .R(Result[3:0]), .C_out(alu4_1_c_out));
  ALU4 alu4_2 (.ALU_Ctrl(ALU_Ctrl), .A(A[7:4]), .B(B[7:4]), .C_in(alu4_1_c_out), .R(Result[7:4]), .C_out(alu4_2_c_out));
  ALU4 alu4_3 (
    .ALU_Ctrl(ALU_Ctrl), .A(A[11:8]), .B(B[11:8]), .C_in(alu4_2_c_out), .R(Result[11:8]), .C_out(alu4_3_c_out));
  ALU4 alu4_4 (
    .ALU_Ctrl(ALU_Ctrl), .A(A[15:12]), .B(B[15:12]), .C_in(alu4_3_c_out), .R(Result[15:12]),
    .C_out(alu4_4_c_out));
  ALU4 alu4_5 (
    .ALU_Ctrl(ALU_Ctrl), .A(A[19:16]), .B(B[19:16]), .C_in(alu4_4_c_out), .R(Result[19:16]),
    .C_out(alu4_5_c_out));
  ALU4 alu4_6 (
    .ALU_Ctrl(ALU_Ctrl), .A(A[23:20]), .B(B[23:20]), .C_in(alu4_5_c_out), .R(Result[23:20]),
    .C_out(alu4_6_c_out));
  ALU4 alu4_7 (
    .ALU_Ctrl(ALU_Ctrl), .A(A[27:24]), .B(B[27:24]), .C_in(alu4_6_c_out), .R(Result[27:24]),
    .C_out(alu4_7_c_out));
  ALU4 alu4_8 (.ALU_Ctrl(ALU_Ctrl), .A(A[31:28]), .B(B[31:28]), .C_in(alu4_7_c_out), .R(Result[31:28]), .C_out(C_out));
endmodule
