// Logisim project lab03.circ as structural Verilog: 11 circuits, main circuit main2
module ALU4 (
  input  [3:0] ALU_Ctrl,
  input  [3:0] A,
  input  [3:0] B,
  input  C_in,
  output [3:0] R,
  output C_out
);

  wire one_bit_alu_1_c_out, one_bit_alu_2_c_out, one_bit_alu_3_c_out;

  one_bit_ALU one_bit_alu_1 (
    .ALU_Ctrl(ALU_Ctrl), .A(A[0]), .B(B[0]), .C_in(C_in), .R(R[0]), .C_out(one_bit_alu_1_c_out));
  one_bit_ALU one_bit_alu_2 (
    .ALU_Ctrl(ALU_Ctrl), .A(A[1]), .B(B[1]), .C_in(one_bit_alu_1_c_out), .R(R[1]), .C_out(one_bit_alu_2_c_out));
  one_bit_ALU one_bit_alu_3 (
    .ALU_Ctrl(ALU_Ctrl), .A(A[2]), .B(B[2]), .C_in(one_bit_alu_2_c_out), .R(R[2]), .C_out(one_bit_alu_3_c_out));
  one_bit_ALU one_bit_alu_4 (
    .ALU_Ctrl(ALU_Ctrl), .A(A[3]), .B(B[3]), .C_in(one_bit_alu_3_c_out), .R(R[3]), .C_out(C_out));
endmodule

module one_bit_adder (
  input  A,
  input  B,
  input  Cin,
  output S,
  output Cout
);

  wire and_1_out, and_2_out, and_3_out, and_4_out, and_5_out, and_6_out, and_7_out, not_1_out, not_2_out,
       not_3_out;

  not not_1 (not_1_out, A);
  not not_2 (not_2_out, B);
  not not_3 (not_3_out, Cin);
  and and_1 (and_1_out, not_1_out, not_2_out, Cin);
  and and_2 (and_2_out, not_1_out, B, not_3_out);
  and and_3 (and_3_out, A, not_2_out, not_3_out);
  and and_4 (and_4_out, A, B, Cin);
  and and_5 (and_5_out, B, Cin);
  and and_6 (and_6_out, A, Cin);
  and and_7 (and_7_out, A, B);
  or or_1 (S, and_1_out, and_2_out, and_3_out, and_4_out);
  or or_2 (Cout, and_5_out, and_6_out, and_7_out);
endmodule

module one_bit_ALU (
  input  [3:0] ALU_Ctrl,
  input  A,
  input  B,
  input  C_in,
  output R,
  output C_out
);

  wire and_1_out, multiplexer_1_out, not_1_out, one_bit_adder_1_s, or_1_out, xor_1_out;

  not not_1 (not_1_out, B);
  Multiplexer #(.enable("false")) multiplexer_1 (.in0(B), .in1(not_1_out), .out(multiplexer_1_out), .sel(ALU_Ctrl[2]));
  and and_1 (and_1_out, A, multiplexer_1_out);
  or or_1 (or_1_out, A, multiplexer_1_out);
  xor xor_1 (xor_1_out, A, multiplexer_1_out);
  one_bit_adder one_bit_adder_1 (.A(A), .B(multiplexer_1_out), .Cin(C_in), .S(one_bit_adder_1_s), .Cout(C_out));
  Multiplexer #(.enable("false"), .select(2)) multiplexer_2 (
    .in0(and_1_out), .in1(or_1_out), .in2(xor_1_out), .in3(one_bit_adder_1_s), .out(R), .sel(ALU_Ctrl[1:0]));
endmodule

module ALU32 (
  input  [3:0] ALU_Ctrl,
  input  [31:0] A,
  input  [31:0] B,
  output [31:0] Result,
  output C_out
);

  wire alu4_1_c_out, alu4_2_c_out, alu4_3_c_out, alu4_4_c_out, alu4_5_c_out, alu4_6_c_out, alu4_7_c_out;

  ALU4 alu4_1 (.ALU_Ctrl(ALU_Ctrl), .A(A[3:0]), .B(B[3:0]), .C_in(ALU_Ctrl[2]), .R(Result[3:0]), .C_out(alu4_1_c_out));
  ALU4 alu4_2 (.ALU_Ctrl(ALU_Ctrl), .A(A[7:4]), .B(B[7:4]), .C_in(alu4_1_c_out), .R(Result[7:4]), .C_out(alu4_2_c_out));
  ALU4 alu4_3 (
    .ALU_Ctrl(ALU_Ctrl), .A(A[11:8]), .B(B[11:8]), .C_in(alu4_2_c_out), .R(Result[11:8]), .C_out(alu4_3_c_out));
  ALU4 alu4_4 (
    .ALU_Ctrl(ALU_Ctrl), .A(A[15:12]), .B(B[15:12]), .C_in(alu4_3_c_out), .R(Result[15:12]),
    .C_out(alu4_4_c_out));
  ALU4 alu4_5 (
    .ALU_Ctrl(ALU_Ctrl), .A(A[19:16]), .B(B[19:16]), .C_in(alu4_4_c_out), .R(Result[19:16]),
    .C_out(alu4_5_c_out));
  ALU4 alu4_6 (
    .ALU_Ctrl(ALU_Ctrl), .A(A[23:20]), .B(B[23:20]), .C_in(alu4_5_c_out), .R(Result[23:20]),
    .C_out(alu4_6_c_out));
  ALU4 alu4_7 (
    .ALU_Ctrl(ALU_Ctrl), .A(A[27:24]), .B(B[27:24]), .C_in(alu4_6_c_out), .R(Result[27:24]),
    .C_out(alu4_7_c_out));
  ALU4 alu4_8 (.ALU_Ctrl(ALU_Ctrl), .A(A[31:28]), .B(B[31:28]), .C_in(alu4_7_c_out), .R(Result[31:28]), .C_out(C_out));

  // Notes on the sheet:
  //   Alyssandra Cordero
endmodule

module ALU_Control (
  input  I30,
  input  I14,
  input  I13,
  input  I12,
  input  I6,
  input  I5,
  input  I4,
  output ALU_Ctrl3,
  output ALU_Ctrl2,
  output ALU_Ctrl1,
  output ALU_Ctrl0,
  output ALU_Src
);

  wire and_2_out, not_1_out, not_2_out, not_3_out, not_4_out, not_5_out;

  not not_1 (not_1_out, I14);
  not not_2 (not_2_out, I13);
  not not_3 (not_3_out, I12);
  not not_4 (not_4_out, I5);
  not not_5 (not_5_out, I4);
  and and_1 (ALU_Ctrl2, I30, not_2_out, I5);
  or or_1 (ALU_Ctrl1, not_2_out, not_5_out);
  and and_2 (and_2_out, I13, not_3_out);
  or or_2 (ALU_Src, not_4_out, not_5_out);
  or or_3 (ALU_Ctrl0, not_1_out, and_2_out);

  assign ALU_Ctrl3 = 1'b0;

  // Notes on the sheet:
  //   Alyssandra Cordero
endmodule

module register_file (
  input  [4:0] RReg1,
  input  [4:0] RReg2,
  input  [31:0] WData,
  input  Clock_in,
  input  Write,
  input  [4:0] Wreg,
  output [31:0] RData1,
  output [31:0] RData2
);

  wire W1, W2, W3, W4, W5, W6, W7, W8, W9, W10, W11, W12, W13, W14, W15, W16, W17, W18, W19, W20, W21, W22,
       W23, W24, W25, W26, W27, W28, W29, W30, W31, W32;
  wire [31:0] Q1, Q2, Q3, Q4, Q5, Q6, Q7, Q8, Q9, Q10, Q11, Q12, Q13, Q14, Q15, Q16, Q17, Q18, Q19, Q20, Q21,
       Q22, Q23, Q24, Q25, Q26, Q27, Q28, Q29, Q30, Q31, Q32;

  Demultiplexer #(.enable("false"), .select(5)) demultiplexer_1 (
    .out0(W1), .out1(W2), .out2(W3), .out3(W4), .out4(W5), .out5(W6), .out6(W7), .out7(W8), .out8(W9),
    .out9(W10), .out10(W11), .out11(W12), .out12(W13), .out13(W14), .out14(W15), .out15(W16), .out16(W17),
    .out17(W18), .out18(W19), .out19(W20), .out20(W21), .out21(W22), .out22(W23), .out23(W24), .out24(W25),
    .out25(W26), .out26(W27), .out27(W28), .out28(W29), .out29(W30), .out30(W31), .out31(W32), .in(Write),
    .sel(Wreg));
  Register #(.width(32)) register_1 (.D(WData), .en(W1), .clk(Clock_in), .Q(Q1), .clr(Write));
  Register #(.width(32)) register_2 (.D(WData), .en(W2), .clk(Clock_in), .Q(Q2));  // open: clr
  Register #(.width(32)) register_3 (.D(WData), .en(W3), .clk(Clock_in), .Q(Q3));  // open: clr
  Register #(.width(32)) register_4 (.D(WData), .en(W4), .clk(Clock_in), .Q(Q4));  // open: clr
  Register #(.width(32)) register_5 (.D(WData), .en(W5), .clk(Clock_in), .Q(Q5));  // open: clr
  Register #(.width(32)) register_6 (.D(WData), .en(W6), .clk(Clock_in), .Q(Q6));  // open: clr
  Register #(.width(32)) register_7 (.D(WData), .en(W7), .clk(Clock_in), .Q(Q7));  // open: clr
  Register #(.width(32)) register_8 (.D(WData), .en(W8), .clk(Clock_in), .Q(Q8));  // open: clr
  Register #(.width(32)) register_9 (.D(WData), .en(W9), .clk(Clock_in), .Q(Q9));  // open: clr
  Register #(.width(32)) register_10 (.D(WData), .en(W10), .clk(Clock_in), .Q(Q10));  // open: clr
  Register #(.width(32)) register_11 (.D(WData), .en(W11), .clk(Clock_in), .Q(Q11));  // open: clr
  Register #(.width(32)) register_12 (.D(WData), .en(W12), .clk(Clock_in), .Q(Q12));  // open: clr
  Register #(.width(32)) register_13 (.D(WData), .en(W13), .clk(Clock_in), .Q(Q13));  // open: clr
  Register #(.width(32)) register_14 (.D(WData), .en(W14), .clk(Clock_in), .Q(Q14));  // open: clr
  Register #(.width(32)) register_15 (.D(WData), .en(W15), .clk(Clock_in), .Q(Q15));  // open: clr
  Register #(.width(32)) register_16 (.D(WData), .en(W16), .clk(Clock_in), .Q(Q16));  // open: clr
  Register #(.width(32)) register_17 (.D(WData), .en(W17), .clk(Clock_in), .Q(Q17));  // open: clr
  Register #(.width(32)) register_18 (.D(WData), .en(W18), .clk(Clock_in), .Q(Q18));  // open: clr
  Register #(.width(32)) register_19 (.D(WData), .en(W19), .clk(Clock_in), .Q(Q19));  // open: clr
  Register #(.width(32)) register_20 (.D(WData), .en(W20), .clk(Clock_in), .Q(Q20));  // open: clr
  Register #(.width(32)) register_21 (.D(WData), .en(W21), .clk(Clock_in), .Q(Q21));  // open: clr
  Register #(.width(32)) register_22 (.D(WData), .en(W22), .clk(Clock_in), .Q(Q22));  // open: clr
  Register #(.width(32)) register_23 (.D(WData), .en(W23), .clk(Clock_in), .Q(Q23));  // open: clr
  Register #(.width(32)) register_24 (.D(WData), .en(W24), .clk(Clock_in), .Q(Q24));  // open: clr
  Register #(.width(32)) register_25 (.D(WData), .en(W25), .clk(Clock_in), .Q(Q25));  // open: clr
  Register #(.width(32)) register_26 (.D(WData), .en(W26), .clk(Clock_in), .Q(Q26));  // open: clr
  Register #(.width(32)) register_27 (.D(WData), .en(W27), .clk(Clock_in), .Q(Q27));  // open: clr
  Register #(.width(32)) register_28 (.D(WData), .en(W28), .clk(Clock_in), .Q(Q28));  // open: clr
  Register #(.width(32)) register_29 (.D(WData), .en(W29), .clk(Clock_in), .Q(Q29));  // open: clr
  Register #(.width(32)) register_30 (.D(WData), .en(W30), .clk(Clock_in), .Q(Q30));  // open: clr
  Register #(.width(32)) register_31 (.D(WData), .en(W31), .clk(Clock_in), .Q(Q31));  // open: clr
  Register #(.width(32)) register_32 (.D(WData), .en(W32), .clk(Clock_in), .Q(Q32));  // open: clr
  Multiplexer #(.enable("false"), .select(5), .width(32)) multiplexer_1 (
    .in0(Q1), .in1(Q2), .in2(Q3), .in3(Q4), .in4(Q5), .in5(Q6), .in6(Q7), .in7(Q8), .in8(Q9), .in9(Q10),
    .in10(Q11), .in11(Q12), .in12(Q13), .in13(Q14), .in14(Q15), .in15(Q16), .in16(Q17), .in17(Q18),
    .in18(Q19), .in19(Q20), .in20(Q21), .in21(Q22), .in22(Q23), .in23(Q24), .in24(Q25), .in25(Q26),
    .in26(Q27), .in27(Q28), .in28(Q29), .in29(Q30), .in30(Q31), .in31(Q32), .out(RData1), .sel(RReg1));
  Multiplexer #(.enable("false"), .select(5), .width(32)) multiplexer_2 (
    .in0(Q1), .in1(Q2), .in2(Q3), .in3(Q4), .in4(Q5), .in5(Q6), .in6(Q7), .in7(Q8), .in8(Q9), .in9(Q10),
    .in10(Q11), .in11(Q12), .in12(Q13), .in13(Q14), .in14(Q15), .in15(Q16), .in16(Q17), .in17(Q18),
    .in18(Q19), .in19(Q20), .in20(Q21), .in21(Q22), .in22(Q23), .in23(Q24), .in24(Q25), .in25(Q26),
    .in26(Q27), .in27(Q28), .in28(Q29), .in29(Q30), .in30(Q31), .in31(Q32), .out(RData2), .sel(RReg2));

  // Notes on the sheet:
  //   Alyssandra Cordero
endmodule

module ImmGen (
  input  [31:0] Instruction,
  output [31:0] IMM32
);

  Multiplexer #(.enable("false"), .width(4)) multiplexer_1 (
    .in0(Instruction[24:21]), .in1(Instruction[11:8]), .out(IMM32[4:1]), .sel(Instruction[5]));
  Multiplexer #(.enable("false")) multiplexer_2 (
    .in0(Instruction[31]), .in1(Instruction[7]), .out(IMM32[11]), .sel(Instruction[6]));
  assign IMM32[31:12] = {{19{Instruction[31]}}, Instruction[31]};  // Bit_Extender bit_extender_1
  Multiplexer #(.enable("false"), .select(2)) multiplexer_3 (
    .in0(Instruction[20]), .in1(Instruction[7]), .in3(1'b0), .out(IMM32[0]), .sel(Instruction[6:5]));  // open: in2

  assign IMM32[10:5] = Instruction[30:25];

  // Other names for the same wires on the sheet: I30_25[5:0] = Instruction[30:25]; I5 = Instruction[5];
  //   I6_5[1:0] = Instruction[6:5]; I6 = Instruction[6]; I7 = Instruction[7]; I11_8[3:0] = Instruction[11:8];
  //   I_20 = Instruction[20]; I24_21[3:0] = Instruction[24:21]; I31 = Instruction[31]

  // Notes on the sheet:
  //   Alyssandra M. Cordero
endmodule

module InstructionMemory (
  input  [23:0] Address,
  input  ClockIn,
  output [31:0] Instruction
);

  wire not_1_out;

  not not_1 (not_1_out, ClockIn);
  RAM #(.addrWidth(22), .asyncread("true"), .dataWidth(32)) ram_1 (
    .addr(Address[23:2]), .we(1'b0), .oe(not_1_out), .dout(Instruction));  // open: clk, din

  // Notes on the sheet:
  //   Alyssandra M. Cordero
endmodule

module DataMemory (
  input  [25:0] Address,
  input  MemWrite,
  input  MemRead,
  input  ClockIn,
  input  [31:0] WriteData,
  output [31:0] ReadData
);

  RAM #(.addrWidth(24), .asyncread("true"), .dataWidth(32)) ram_1 (
    .addr(Address[25:2]), .we(MemWrite), .oe(MemRead), .clk(ClockIn), .din(WriteData), .dout(ReadData));

  // Notes on the sheet:
  //   Alyssandra M. Cordero
endmodule

module Control (
  input  [6:0] I6_0,
  output MemtoReg,
  output RegWrite,
  output MemRead,
  output MemWrite,
  output Branch
);

  wire not_1_out, not_2_out;

  not not_1 (not_1_out, I6_0[6]);
  not not_2 (not_2_out, I6_0[5]);
  not not_3 (MemtoReg, I6_0[4]);
  or or_1 (RegWrite, not_2_out, I6_0[4]);
  and and_1 (MemRead, not_2_out, MemtoReg);
  and and_2 (MemWrite, not_1_out, I6_0[5], MemtoReg);

  assign Branch = I6_0[6];

  // Notes on the sheet:
  //   Alyssandra M. Cordero
endmodule

module main2 (
);

  wire alu_control_1_alu_src, and_1_out, clock_1_out, comparator_1_eq, control_1_branch, control_1_memread,
       control_1_memtoreg, control_1_memwrite, control_1_regwrite;
  wire [3:0] alu_control_1_alu_ctrl0;
  wire [31:0] adder_1_out, adder_2_out, alu32_1_result, datamemory_1_readdata, immgen_1_imm32,
       instructionmemory_1_instruction, multiplexer_1_out, multiplexer_2_out, multiplexer_3_out,
       register_1_q, register_file_1_rdata1, register_file_1_rdata2;

  Register #(.width(32)) register_1 (
    .D(multiplexer_2_out), .en(1'b1), .clk(clock_1_out), .Q(register_1_q));  // open: clr
  Adder #(.width(32)) adder_1 (.a(register_1_q), .b(32'h4), .out(adder_1_out));  // open: cin, cout
  Clock clock_1 (.out(clock_1_out));
  InstructionMemory instructionmemory_1 (
    .Address(register_1_q[23:0]), .ClockIn(clock_1_out), .Instruction(instructionmemory_1_instruction));
  ImmGen immgen_1 (.Instruction(instructionmemory_1_instruction), .IMM32(immgen_1_imm32));
  Control control_1 (
    .I6_0(instructionmemory_1_instruction[6:0]), .MemtoReg(control_1_memtoreg),
    .RegWrite(control_1_regwrite), .MemRead(control_1_memread), .MemWrite(control_1_memwrite),
    .Branch(control_1_branch));
  register_file register_file_1 (
    .RReg1(instructionmemory_1_instruction[19:15]), .RReg2(instructionmemory_1_instruction[24:20]),
    .WData(multiplexer_3_out), .Clock_in(clock_1_out), .Write(control_1_regwrite),
    .Wreg(instructionmemory_1_instruction[11:7]), .RData1(register_file_1_rdata1),
    .RData2(register_file_1_rdata2));
  Multiplexer #(.enable("false"), .width(32)) multiplexer_1 (
    .in0(register_file_1_rdata2), .in1(immgen_1_imm32), .out(multiplexer_1_out), .sel(alu_control_1_alu_src));
  ALU_Control alu_control_1 (
    .I30(instructionmemory_1_instruction[30]), .I14(instructionmemory_1_instruction[14]),
    .I13(instructionmemory_1_instruction[13]), .I12(instructionmemory_1_instruction[12]),
    .I6(instructionmemory_1_instruction[6]), .I5(instructionmemory_1_instruction[5]),
    .I4(instructionmemory_1_instruction[4]), .ALU_Ctrl3(alu_control_1_alu_ctrl0[3]),
    .ALU_Ctrl2(alu_control_1_alu_ctrl0[2]), .ALU_Ctrl1(alu_control_1_alu_ctrl0[1]),
    .ALU_Ctrl0(alu_control_1_alu_ctrl0[0]), .ALU_Src(alu_control_1_alu_src));
  Adder #(.width(32)) adder_2 (.a(register_1_q), .b(immgen_1_imm32), .out(adder_2_out));  // open: cin, cout
  Comparator #(.width(32)) comparator_1 (
    .a(register_file_1_rdata1), .b(register_file_1_rdata2), .eq(comparator_1_eq));  // open: gt, lt
  ALU32 alu32_1 (
    .ALU_Ctrl(alu_control_1_alu_ctrl0), .A(register_file_1_rdata1), .B(multiplexer_1_out),
    .Result(alu32_1_result));  // open: C_out
  Multiplexer #(.enable("false"), .width(32)) multiplexer_2 (
    .in0(adder_1_out), .in1(adder_2_out), .out(multiplexer_2_out), .sel(and_1_out));
  and and_1 (and_1_out, control_1_branch, comparator_1_eq);
  Multiplexer #(.enable("false"), .width(32)) multiplexer_3 (
    .in0(alu32_1_result), .in1(datamemory_1_readdata), .out(multiplexer_3_out), .sel(control_1_memtoreg));
  DataMemory datamemory_1 (
    .Address(alu32_1_result[25:0]), .MemWrite(control_1_memwrite), .MemRead(control_1_memread),
    .ClockIn(clock_1_out), .WriteData(register_file_1_rdata2), .ReadData(datamemory_1_readdata));

  // Notes on the sheet:
  //   Alyssandra M. Cordero
endmodule
